// Logisim project D锁存器.circ as structural Verilog: 2 circuits, main circuit D
module D (
  input  D,
  input  CP,
  output Q,
  output QN
);

  wire nand_1_out, nand_2_out, not_1_out;

  not not_1 (not_1_out, D);
  nand nand_1 (nand_1_out, D, CP);
  nand nand_2 (nand_2_out, CP, not_1_out);
  nand nand_3 (Q, nand_1_out, QN);
  nand nand_4 (QN, nand_2_out, Q);
endmodule

module DD (
  input  in_1,
  input  in_2,
  output out_3,
  output out_4
);

  wire d_1_q, not_1_out;

  not not_1 (not_1_out, in_1);
  D d_1 (.D(in_2), .CP(in_1), .Q(d_1_q));  // open: QN
  D d_2 (.D(d_1_q), .CP(not_1_out), .Q(out_3), .QN(out_4));
endmodule
