// Logisim project GRF.circ as structural Verilog: 1 circuit, main circuit grf
module grf (
  input  clk,
  input  reset,
  input  WE,
  input  [4:0] A1,
  input  [4:0] A2,
  input  [4:0] A3,
  input  [31:0] WD,
  output [31:0] RO1,
  output [31:0] RO2
);

  wire [31:0] _1, _1_t, _2, _2_t, _3, _3_t, _4, _4_t, _5, _5_t, _6, _6_t, _7, _7_t, _8, _8_t, _9, _9_t, _10,
       _10_t, _11, _11_t, _12, _12_t, _13, _13_t, _14, _14_t, _15, _15_t, _16, _16_t, _17, _17_t, _18, _18_t,
       _19, _19_t, _20, _20_t, _21, _21_t, _22, _22_t, _23, _23_t, _24, _24_t, _25, _25_t, _26, _26_t, _27,
       _27_t, _28, _28_t, _29, _29_t, _30, _30_t, _31, _31_t;

  Register #(.width(32)) register_1 (.D({32{1'b0}}), .en(reset), .clk(clk), .clr(WE));  // open: Q
  Register #(.width(32)) register_2 (.D(_8_t), .en(WE), .Q(_8), .clk(clk), .clr(reset));
  Register #(.width(32)) register_3 (.D(_16_t), .en(WE), .Q(_16), .clk(clk), .clr(reset));
  Register #(.width(32)) register_4 (.D(_24_t), .en(WE), .Q(_24), .clk(clk), .clr(reset));
  Register #(.width(32)) register_5 (.D(_1_t), .en(WE), .Q(_1), .clk(clk), .clr(reset));
  Register #(.width(32)) register_6 (.D(_9_t), .en(WE), .Q(_9), .clk(clk), .clr(reset));
  Register #(.width(32)) register_7 (.D(_17_t), .en(WE), .Q(_17), .clk(clk), .clr(reset));
  Register #(.width(32)) register_8 (.D(_25_t), .en(WE), .Q(_25), .clk(clk), .clr(reset));
  Register #(.width(32)) register_9 (.D(_2_t), .en(WE), .Q(_2), .clk(clk), .clr(reset));
  Register #(.width(32)) register_10 (.D(_10_t), .en(WE), .Q(_10), .clk(clk), .clr(reset));
  Register #(.width(32)) register_11 (.D(_18_t), .en(WE), .Q(_18), .clk(clk), .clr(reset));
  Register #(.width(32)) register_12 (.D(_26_t), .en(WE), .Q(_26), .clk(clk), .clr(reset));
  Register #(.width(32)) register_13 (.D(_3_t), .en(WE), .Q(_3), .clk(clk), .clr(reset));
  Register #(.width(32)) register_14 (.D(_11_t), .en(WE), .Q(_11), .clk(clk), .clr(reset));
  Register #(.width(32)) register_15 (.D(_19_t), .en(WE), .Q(_19), .clk(clk), .clr(reset));
  Register #(.width(32)) register_16 (.D(_27_t), .en(WE), .Q(_27), .clk(clk), .clr(reset));
  Demultiplexer #(.select(5), .width(32), .tristate("true"), .enable("false")) demultiplexer_1 (
    .out1(_1_t), .out2(_2_t), .out3(_3_t), .out4(_4_t), .out5(_5_t), .out6(_6_t), .out7(_7_t), .out8(_8_t),
    .out9(_9_t), .out10(_10_t), .out11(_11_t), .out12(_12_t), .out13(_13_t), .out14(_14_t), .out15(_15_t),
    .out16(_16_t), .out17(_17_t), .out18(_18_t), .out19(_19_t), .out20(_20_t), .out21(_21_t), .out22(_22_t),
    .out23(_23_t), .out24(_24_t), .out25(_25_t), .out26(_26_t), .out27(_27_t), .out28(_28_t), .out29(_29_t),
    .out30(_30_t), .out31(_31_t), .in(WD), .sel(A3));  // open: out0
  Register #(.width(32)) register_17 (.D(_4_t), .en(WE), .Q(_4), .clk(clk), .clr(reset));
  Register #(.width(32)) register_18 (.D(_12_t), .en(WE), .Q(_12), .clk(clk), .clr(reset));
  Register #(.width(32)) register_19 (.D(_20_t), .en(WE), .Q(_20), .clk(clk), .clr(reset));
  Register #(.width(32)) register_20 (.D(_28_t), .en(WE), .Q(_28), .clk(clk), .clr(reset));
  Register #(.width(32)) register_21 (.D(_5_t), .en(WE), .Q(_5), .clk(clk), .clr(reset));
  Register #(.width(32)) register_22 (.D(_13_t), .en(WE), .Q(_13), .clk(clk), .clr(reset));
  Register #(.width(32)) register_23 (.D(_21_t), .en(WE), .Q(_21), .clk(clk), .clr(reset));
  Register #(.width(32)) register_24 (.D(_29_t), .en(WE), .Q(_29), .clk(clk), .clr(reset));
  Register #(.width(32)) register_25 (.D(_6_t), .en(WE), .Q(_6), .clk(clk), .clr(reset));
  Register #(.width(32)) register_26 (.D(_14_t), .en(WE), .Q(_14), .clk(clk), .clr(reset));
  Register #(.width(32)) register_27 (.D(_22_t), .en(WE), .Q(_22), .clk(clk), .clr(reset));
  Register #(.width(32)) register_28 (.D(_30_t), .en(WE), .Q(_30), .clk(clk), .clr(reset));
  Register #(.width(32)) register_29 (.D(_7_t), .en(WE), .Q(_7), .clk(clk), .clr(reset));
  Register #(.width(32)) register_30 (.D(_15_t), .en(WE), .Q(_15), .clk(clk), .clr(reset));
  Register #(.width(32)) register_31 (.D(_23_t), .en(WE), .Q(_23), .clk(clk), .clr(reset));
  Register #(.width(32)) register_32 (.D(_31_t), .en(WE), .Q(_31), .clk(clk), .clr(reset));
  Multiplexer #(.select(5), .width(32), .enable("false")) multiplexer_1 (
    .in0({32{1'b0}}), .in1(_1), .in2(_2), .in3(_3), .in4(_4), .in5(_5), .in6(_6), .in7(_7), .in8(_8),
    .in9(_9), .in10(_10), .in11(_11), .in12(_12), .in13(_13), .in14(_14), .in15(_15), .in16(_16), .in17(_17),
    .in18(_18), .in19(_19), .in20(_20), .in21(_21), .in22(_22), .in23(_23), .in24(_24), .in25(_25),
    .in26(_26), .in27(_27), .in28(_28), .in29(_29), .in30(_30), .in31(_31), .out(RO1), .sel(A1));
  Multiplexer #(.select(5), .width(32), .enable("false")) multiplexer_2 (
    .in0({32{1'b0}}), .in1(_1), .in2(_2), .in3(_3), .in4(_4), .in5(_5), .in6(_6), .in7(_7), .in8(_8),
    .in9(_9), .in10(_10), .in11(_11), .in12(_12), .in13(_13), .in14(_14), .in15(_15), .in16(_16), .in17(_17),
    .in18(_18), .in19(_19), .in20(_20), .in21(_21), .in22(_22), .in23(_23), .in24(_24), .in25(_25),
    .in26(_26), .in27(_27), .in28(_28), .in29(_29), .in30(_30), .in31(_31), .out(RO2), .sel(A2));

  // Other names for the same wires on the sheet: c = clk; r = reset; w = WE
endmodule
