// Logisim project P0.4.2.circ as structural Verilog: 3 circuits, main circuit fsm
module fsm (
  input  in_1,
  input  [1:0] in_2,
  output out_3
);

  wire a_1_x, a_1_y, and_1_out, and_2_out, clock_1_out, not_1_out, register_1_q, register_2_q;

  not not_1 (not_1_out, in_1);
  and and_1 (and_1_out, not_1_out, a_1_x);
  a a_1 (.a(register_1_q), .b(register_2_q), .c(in_2[1]), .d(in_2[0]), .x(a_1_x), .y(a_1_y));
  Clock clock_1 (.out(clock_1_out));
  and and_2 (and_2_out, a_1_y, not_1_out);
  Register #(.width(1)) register_1 (.D(and_1_out), .Q(register_1_q), .clk(clock_1_out));  // open: en, clr
  Register #(.width(1)) register_2 (.D(and_2_out), .Q(register_2_q), .clk(clock_1_out));  // open: en, clr
  b b_1 (.a(register_1_q), .b(register_2_q), .c(in_2[1]), .d(in_2[0]), .c_2(out_3));
endmodule

module a (
  input  a,
  input  b,
  input  c,
  input  d,
  output x,
  output y
);

  wire and_1_out, and_2_out, and_3_out, and_4_out, not_1_out, not_2_out, not_3_out, not_4_out, not_5_out,
       not_6_out, not_7_out;

  not not_1 (not_1_out, a);
  and and_1 (and_1_out, not_1_out, b, not_2_out);
  not not_2 (not_2_out, d);
  not not_3 (not_3_out, b);
  and and_2 (and_2_out, a, not_3_out, not_4_out);
  not not_4 (not_4_out, d);
  not not_5 (not_5_out, c);
  and and_3 (and_3_out, not_5_out, d);
  not not_6 (not_6_out, b);
  and and_4 (and_4_out, a, not_6_out, not_7_out);
  not not_7 (not_7_out, d);
  or or_1 (x, and_1_out, and_2_out);
  or or_2 (y, and_3_out, and_4_out);
endmodule

module b (
  input  a,
  input  b,
  input  c,
  input  d,
  output c_2
);

  wire not_1_out, not_2_out;

  and and_1 (c_2, a, not_1_out, not_2_out);
  not not_1 (not_1_out, b);
  not not_2 (not_2_out, d);
endmodule
