// Logisim project dispenser.circ as structural Verilog: 3 circuits, main circuit dispenser
module dispenser (
  input  [1:0] money,
  input  reset,
  output dispense,
  output return4,
  output return2,
  output return1
);

  wire clock_1_out, not_1_out, or_1_out, register_2_q;
  wire [3:0] n1_1_cc, register_1_q;

  Clock clock_1 (.out(clock_1_out));
  _1 u_1_1 (
    .a(money[0]), .b(money[1]), .c(register_1_q[0]), .d(register_1_q[1]), .e(register_1_q[2]),
    .f(register_1_q[3]), .cc(n1_1_cc[0]), .dd(n1_1_cc[1]), .ee(n1_1_cc[2]), .ff(n1_1_cc[3]));
  or or_1 (or_1_out, reset, register_2_q);
  Register #(.width(4)) register_1 (.D(n1_1_cc), .Q(register_1_q), .clk(clock_1_out), .clr(or_1_out));  // open: en
  _2 u_2_1 (
    .c(register_1_q[0]), .d(register_1_q[1]), .e(register_1_q[2]), .f(register_1_q[3]), .x(dispense),
    .y(return4), .z(return2), .u(return1));
  not not_1 (not_1_out, dispense);
  Register #(.width(1)) register_2 (.D(dispense), .Q(register_2_q), .clk(clock_1_out), .clr(not_1_out));  // open: en
endmodule

module _1 (
  input  a,
  input  b,
  input  c,
  input  d,
  input  e,
  input  f,
  output cc,
  output dd,
  output ee,
  output ff
);

  wire and_2_out, and_3_out, and_4_out, and_5_out, and_6_out, and_7_out, and_8_out, and_9_out, and_10_out,
       and_11_out, and_12_out, and_13_out, and_14_out, not_1_out, not_2_out, not_3_out, not_4_out, not_5_out,
       not_6_out, not_7_out, not_8_out, not_9_out, not_10_out, not_11_out, not_12_out, not_13_out,
       not_14_out, not_15_out, not_16_out;

  not not_1 (not_1_out, a);
  not not_2 (not_2_out, c);
  not not_3 (not_3_out, a);
  not not_4 (not_4_out, b);
  not not_5 (not_5_out, a);
  not not_6 (not_6_out, d);
  not not_7 (not_7_out, c);
  not not_8 (not_8_out, d);
  not not_9 (not_9_out, a);
  not not_10 (not_10_out, b);
  not not_11 (not_11_out, a);
  not not_12 (not_12_out, b);
  not not_13 (not_13_out, c);
  not not_14 (not_14_out, e);
  not not_15 (not_15_out, d);
  not not_16 (not_16_out, e);
  and and_1 (ff, a, b, e);
  and and_2 (and_2_out, not_1_out, c);
  and and_3 (and_3_out, a, not_2_out);
  and and_4 (and_4_out, a, b, d);
  and and_5 (and_5_out, not_3_out, not_4_out, d);
  and and_6 (and_6_out, not_5_out, b, not_6_out);
  and and_7 (and_7_out, a, not_7_out, d);
  and and_8 (and_8_out, a, c, not_8_out);
  and and_9 (and_9_out, not_9_out, e);
  and and_10 (and_10_out, not_10_out, e);
  and and_11 (and_11_out, not_11_out, b, d);
  and and_12 (and_12_out, a, not_12_out, c, d);
  and and_13 (and_13_out, a, b, not_13_out, not_14_out);
  and and_14 (and_14_out, a, b, not_15_out, not_16_out);
  or or_1 (cc, and_2_out, and_3_out, and_4_out);
  or or_2 (dd, and_5_out, and_6_out, and_7_out, and_8_out);
  or or_3 (ee, and_9_out, and_10_out, and_11_out, and_12_out, and_13_out, and_14_out);
endmodule

module _2 (
  input  c,
  input  d,
  input  e,
  input  f,
  output x,
  output y,
  output z,
  output u
);

  wire and_1_out, and_2_out, and_3_out, and_5_out, and_6_out, and_7_out, and_8_out, not_1_out, not_2_out,
       not_3_out, not_4_out, not_5_out, not_6_out, not_7_out, not_8_out, not_9_out, not_10_out, not_11_out,
       not_12_out, not_13_out, not_14_out, not_15_out;

  not not_1 (not_1_out, d);
  and and_1 (and_1_out, not_1_out, not_2_out, f);
  not not_2 (not_2_out, e);
  and and_2 (and_2_out, d, e, not_3_out);
  not not_3 (not_3_out, f);
  and and_3 (and_3_out, c, e, not_4_out);
  not not_4 (not_4_out, f);
  not not_5 (not_5_out, d);
  not not_6 (not_6_out, e);
  not not_7 (not_7_out, c);
  not not_8 (not_8_out, d);
  not not_9 (not_9_out, e);
  not not_10 (not_10_out, f);
  not not_11 (not_11_out, c);
  not not_12 (not_12_out, d);
  not not_13 (not_13_out, e);
  not not_14 (not_14_out, c);
  not not_15 (not_15_out, f);
  or or_1 (x, and_1_out, and_2_out, and_3_out);
  and and_4 (y, c, not_5_out, not_6_out, f);
  and and_5 (and_5_out, not_7_out, not_8_out, not_9_out, f);
  or or_2 (z, and_5_out, and_6_out);
  and and_6 (and_6_out, c, d, e, not_10_out);
  and and_7 (and_7_out, not_11_out, not_12_out, not_13_out, f);
  or or_3 (u, and_7_out, and_8_out);
  and and_8 (and_8_out, not_14_out, d, e, not_15_out);
endmodule
