// Logisim project 抢答器.circ as structural Verilog: 1 circuit, main circuit main
module main (
  input  A,
  input  B,
  input  C,
  input  J,
  output a_2,
  output b_2,
  output c_2
);

  wire clock_1_out, d_ff_1_qn, d_ff_2_qn, d_ff_3_qn, nand_1_out;

  D_Flip_Flop d_ff_1 (.clk(nand_1_out), .D(A), .Q(a_2), .Qn(d_ff_1_qn), .reset(J));  // open: preset, en
  D_Flip_Flop d_ff_2 (.clk(nand_1_out), .D(B), .Q(b_2), .Qn(d_ff_2_qn), .reset(J));  // open: preset, en
  D_Flip_Flop d_ff_3 (.clk(nand_1_out), .D(C), .Q(c_2), .Qn(d_ff_3_qn), .reset(J));  // open: preset, en
  Clock clock_1 (.out(clock_1_out));
  nand nand_1 (nand_1_out, d_ff_1_qn, d_ff_2_qn, d_ff_3_qn, clock_1_out);
endmodule
