// Logisim project p3_zz.circ as structural Verilog: 8 circuits, main circuit main
module main (
  input  reset,
  output [31:0] out_2,
  output out_3,
  output [4:0] out_4,
  output [31:0] out_5,
  output out_6,
  output [4:0] out_7,
  output [31:0] out_8
);

  wire alu_1_zero, and_1_out, CLK, controller_1_branch, controller_1_memread, controller_1_memtoreg,
       controller_1_regdst;
  wire [1:0] controller_1_alusrc;
  wire [3:0] controller_1_aluop;
  wire [4:0] ifu_1_rd, ifu_1_rs, ifu_1_rt;
  wire [5:0] ifu_1_func, ifu_1_op;
  wire [15:0] ifu_1_imm;
  wire [31:0] alu_1_result, dm_1_readdata, ext_1__0_ext, ext_1_shift2, ext_1_shift16, ext_1_sign_ext,
       grf_1_readdata1, ifu_1_pcout, multiplexer_2_out, pcadd_1_pc_plus;

  // Probe on grf_1_readdata1
  // Probe on ifu_1_rs
  // Probe on ifu_1_rt
  // Probe on ifu_1_rd
  IFU ifu_1 (
    .PCin(pcadd_1_pc_plus), .clk(CLK), .reset(reset), .PCout(ifu_1_pcout), .instr(out_2), .Func(ifu_1_func),
    .Rd(ifu_1_rd), .Rt(ifu_1_rt), .Rs(ifu_1_rs), .op(ifu_1_op), .imm(ifu_1_imm));  // open: shamt
  // Probe on ifu_1_imm
  // Probe on ifu_1_op
  // Probe on ifu_1_func
  Controller controller_1 (
    .op(ifu_1_op), .func(ifu_1_func), .RegWrite(out_3), .MemRead(controller_1_memread), .MemWrite(out_6),
    .RegDst(controller_1_regdst), .branch(controller_1_branch), .MemtoReg(controller_1_memtoreg),
    .ALUSrc(controller_1_alusrc), .ALUop(controller_1_aluop));
  // Probe on controller_1_alusrc
  // Probe on controller_1_aluop
  Clock clock_1 (.out(CLK));
  Multiplexer #(.width(5), .enable("false")) multiplexer_1 (
    .in0(ifu_1_rt), .in1(ifu_1_rd), .out(out_4), .sel(controller_1_regdst));
  GRF grf_1 (
    .reset(reset), .RegWrite(out_3), .Rs(ifu_1_rs), .Rt(ifu_1_rt), .Rd(out_4), .WD(out_5), .clk(CLK),
    .Readdata1(grf_1_readdata1), .Readdata2(out_8));
  EXT ext_1 (
    .imm(ifu_1_imm), ._0_ext(ext_1__0_ext), .sign_ext(ext_1_sign_ext), .shift2(ext_1_shift2),
    .shift16(ext_1_shift16));
  PCadd pcadd_1 (.PC(ifu_1_pcout), .shift2(ext_1_shift2), .PCsrc(and_1_out), .PC_plus(pcadd_1_pc_plus));
  and and_1 (and_1_out, controller_1_branch, alu_1_zero);
  Multiplexer #(.select(2), .width(32), .enable("false")) multiplexer_2 (
    .in0(out_8), .in1(ext_1_sign_ext), .in2(ext_1__0_ext), .in3(ext_1_shift16), .out(multiplexer_2_out),
    .sel(controller_1_alusrc));
  ALU alu_1 (
    .A(grf_1_readdata1), .B(multiplexer_2_out), .ALUop(controller_1_aluop), .Zero(alu_1_zero),
    .result(alu_1_result));
  DM dm_1 (
    .Address(alu_1_result), .Writedata(out_8), .clk(CLK), .Reset(reset), .memwrite(out_6),
    .memread(controller_1_memread), .MemAddr(out_7), .Readdata(dm_1_readdata));
  Multiplexer #(.width(32), .enable("false")) multiplexer_3 (
    .in0(alu_1_result), .in1(dm_1_readdata), .out(out_5), .sel(controller_1_memtoreg));
  // Probe on pcadd_1_pc_plus
  // Probe on alu_1_result
  // Probe on multiplexer_2_out

  // Other names for the same wires on the sheet: Instr[31:0] = out_2; MemAddr[4:0] = out_7; MemData[31:0] = out_8;
  //   MemWrite = out_6; RegAddr[4:0] = out_4; RegData[31:0] = out_5; RegWrite = out_3
endmodule

module IFU (
  input  [31:0] PCin,
  input  clk,
  input  reset,
  output [5:0] Func,
  output [4:0] shamt,
  output [31:0] PCout,
  output [4:0] Rd,
  output [4:0] Rt,
  output [4:0] Rs,
  output [5:0] op,
  output [15:0] imm,
  output [31:0] instr
);

  Register #(.width(32)) PC (.D(PCin), .Q(PCout), .clk(clk), .clr(reset));  // open: en
  ROM #(.addrWidth(5), .dataWidth(32)) rom_1 (.addr(PCout[6:2]), .data({instr[31:16], imm[15:6], Func}));  // open: sel

  assign imm[5:0] = Func;
  assign instr[15:0] = {imm[15:6], Func};
  assign op = instr[31:26];
  assign Rd = imm[15:11];
  assign Rs = instr[25:21];
  assign Rt = instr[20:16];
  assign shamt = imm[10:6];

  // Notes on the sheet:
  //   IM
  //   contents of rom_1 (hex, n*v repeats v):
  //   34090005 340a0003 352b0004 12a4021 12a4023 112a0001 3c1004d2 8d0d0000 ad2d0000
endmodule

module GRF (
  input  reset,
  input  RegWrite,
  input  [4:0] Rs,
  input  [4:0] Rt,
  input  [4:0] Rd,
  input  [31:0] WD,
  input  clk,
  output [31:0] Readdata1,
  output [31:0] Readdata2
);

  wire [31:0] _1, _1_t, _2, _2_t, _3, _3_t, _4, _4_t, _5, _5_t, _6, _6_t, _7, _7_t, _8, _8_t, _9, _9_t, _10,
       _10_t, _11, _11_t, _12, _12_t, _13, _13_t, _14, _14_t, _15, _15_t, _16, _16_t, _17, _17_t, _18, _18_t,
       _19, _19_t, _20, _20_t, _21, _21_t, _22, _22_t, _23, _23_t, _24, _24_t, _25, _25_t, _26, _26_t, _27,
       _27_t, _28, _28_t, _29, _29_t, _30, _30_t, _31, _31_t;

  Register #(.width(32)) register_1 (.D({32{1'b0}}), .en(RegWrite), .clk(clk), .clr(reset));  // open: Q
  Register #(.width(32)) register_2 (.D(_8_t), .en(RegWrite), .Q(_8), .clk(clk), .clr(reset));
  Register #(.width(32)) register_3 (.D(_16_t), .en(RegWrite), .Q(_16), .clk(clk), .clr(reset));
  Register #(.width(32)) register_4 (.D(_24_t), .en(RegWrite), .Q(_24), .clk(clk), .clr(reset));
  Register #(.width(32)) register_5 (.D(_1_t), .en(RegWrite), .Q(_1), .clk(clk), .clr(reset));
  Register #(.width(32)) register_6 (.D(_9_t), .en(RegWrite), .Q(_9), .clk(clk), .clr(reset));
  Register #(.width(32)) register_7 (.D(_17_t), .en(RegWrite), .Q(_17), .clk(clk), .clr(reset));
  Register #(.width(32)) register_8 (.D(_25_t), .en(RegWrite), .Q(_25), .clk(clk), .clr(reset));
  Register #(.width(32)) register_9 (.D(_2_t), .en(RegWrite), .Q(_2), .clk(clk), .clr(reset));
  Register #(.width(32)) register_10 (.D(_10_t), .en(RegWrite), .Q(_10), .clk(clk), .clr(reset));
  Register #(.width(32)) register_11 (.D(_18_t), .en(RegWrite), .Q(_18), .clk(clk), .clr(reset));
  Register #(.width(32)) register_12 (.D(_26_t), .en(RegWrite), .Q(_26), .clk(clk), .clr(reset));
  Register #(.width(32)) register_13 (.D(_3_t), .en(RegWrite), .Q(_3), .clk(clk), .clr(reset));
  Register #(.width(32)) register_14 (.D(_11_t), .en(RegWrite), .Q(_11), .clk(clk), .clr(reset));
  Register #(.width(32)) register_15 (.D(_19_t), .en(RegWrite), .Q(_19), .clk(clk), .clr(reset));
  Register #(.width(32)) register_16 (.D(_27_t), .en(RegWrite), .Q(_27), .clk(clk), .clr(reset));
  Demultiplexer #(.select(5), .width(32), .tristate("true"), .enable("false")) demultiplexer_1 (
    .out1(_1_t), .out2(_2_t), .out3(_3_t), .out4(_4_t), .out5(_5_t), .out6(_6_t), .out7(_7_t), .out8(_8_t),
    .out9(_9_t), .out10(_10_t), .out11(_11_t), .out12(_12_t), .out13(_13_t), .out14(_14_t), .out15(_15_t),
    .out16(_16_t), .out17(_17_t), .out18(_18_t), .out19(_19_t), .out20(_20_t), .out21(_21_t), .out22(_22_t),
    .out23(_23_t), .out24(_24_t), .out25(_25_t), .out26(_26_t), .out27(_27_t), .out28(_28_t), .out29(_29_t),
    .out30(_30_t), .out31(_31_t), .in(WD), .sel(Rd));  // open: out0
  Register #(.width(32)) register_17 (.D(_4_t), .en(RegWrite), .Q(_4), .clk(clk), .clr(reset));
  Register #(.width(32)) register_18 (.D(_12_t), .en(RegWrite), .Q(_12), .clk(clk), .clr(reset));
  Register #(.width(32)) register_19 (.D(_20_t), .en(RegWrite), .Q(_20), .clk(clk), .clr(reset));
  Register #(.width(32)) register_20 (.D(_28_t), .en(RegWrite), .Q(_28), .clk(clk), .clr(reset));
  Register #(.width(32)) register_21 (.D(_5_t), .en(RegWrite), .Q(_5), .clk(clk), .clr(reset));
  Register #(.width(32)) register_22 (.D(_13_t), .en(RegWrite), .Q(_13), .clk(clk), .clr(reset));
  Register #(.width(32)) register_23 (.D(_21_t), .en(RegWrite), .Q(_21), .clk(clk), .clr(reset));
  Register #(.width(32)) register_24 (.D(_29_t), .en(RegWrite), .Q(_29), .clk(clk), .clr(reset));
  Register #(.width(32)) register_25 (.D(_6_t), .en(RegWrite), .Q(_6), .clk(clk), .clr(reset));
  Register #(.width(32)) register_26 (.D(_14_t), .en(RegWrite), .Q(_14), .clk(clk), .clr(reset));
  Register #(.width(32)) register_27 (.D(_22_t), .en(RegWrite), .Q(_22), .clk(clk), .clr(reset));
  Register #(.width(32)) register_28 (.D(_30_t), .en(RegWrite), .Q(_30), .clk(clk), .clr(reset));
  Register #(.width(32)) register_29 (.D(_7_t), .en(RegWrite), .Q(_7), .clk(clk), .clr(reset));
  Register #(.width(32)) register_30 (.D(_15_t), .en(RegWrite), .Q(_15), .clk(clk), .clr(reset));
  Register #(.width(32)) register_31 (.D(_23_t), .en(RegWrite), .Q(_23), .clk(clk), .clr(reset));
  Register #(.width(32)) register_32 (.D(_31_t), .en(RegWrite), .Q(_31), .clk(clk), .clr(reset));
  Multiplexer #(.select(5), .width(32), .enable("false")) multiplexer_1 (
    .in0({32{1'b0}}), .in1(_1), .in2(_2), .in3(_3), .in4(_4), .in5(_5), .in6(_6), .in7(_7), .in8(_8),
    .in9(_9), .in10(_10), .in11(_11), .in12(_12), .in13(_13), .in14(_14), .in15(_15), .in16(_16), .in17(_17),
    .in18(_18), .in19(_19), .in20(_20), .in21(_21), .in22(_22), .in23(_23), .in24(_24), .in25(_25),
    .in26(_26), .in27(_27), .in28(_28), .in29(_29), .in30(_30), .in31(_31), .out(Readdata1), .sel(Rs));
  Multiplexer #(.select(5), .width(32), .enable("false")) multiplexer_2 (
    .in0({32{1'b0}}), .in1(_1), .in2(_2), .in3(_3), .in4(_4), .in5(_5), .in6(_6), .in7(_7), .in8(_8),
    .in9(_9), .in10(_10), .in11(_11), .in12(_12), .in13(_13), .in14(_14), .in15(_15), .in16(_16), .in17(_17),
    .in18(_18), .in19(_19), .in20(_20), .in21(_21), .in22(_22), .in23(_23), .in24(_24), .in25(_25),
    .in26(_26), .in27(_27), .in28(_28), .in29(_29), .in30(_30), .in31(_31), .out(Readdata2), .sel(Rt));

  // Other names for the same wires on the sheet: RO1[31:0] = Readdata1; RO2[31:0] = Readdata2
endmodule

module ALU (
  input  [31:0] A,
  input  [31:0] B,
  input  [3:0] ALUop,
  output Zero,
  output [31:0] result
);

  wire [31:0] adder_1_out, and_1_out, or_1_out, subtractor_1_out;

  assign or_1_out = A | B;  // OR_Gate or_1, 32 bits wide
  assign and_1_out = A & B;  // AND_Gate and_1, 32 bits wide
  Adder #(.width(32)) adder_1 (.a(A), .b(B), .out(adder_1_out));  // open: cin, cout
  Subtractor #(.width(32)) subtractor_1 (.a(A), .b(B), .out(subtractor_1_out));  // open: bin, bout
  Comparator #(.width(32)) comparator_1 (.a(A), .b(B), .eq(Zero));  // open: gt, lt
  Multiplexer #(.select(4), .width(32), .enable("false")) multiplexer_1 (
    .in0(and_1_out), .in1(or_1_out), .in2(adder_1_out), .in6(subtractor_1_out), .out(result), .sel(ALUop));  // open: in3, in4, in5, in7, in8, in9, in10, in11, in12, in13, in14, in15
endmodule

module DM (
  input  [31:0] Address,
  input  [31:0] Writedata,
  input  clk,
  input  Reset,
  input  memwrite,
  input  memread,
  output [4:0] MemAddr,
  output [31:0] Readdata
);

  RAM #(.addrWidth(5), .dataWidth(32), .bus("separate")) ram_1 (
    .addr(Address[6:2]), .din(Writedata), .data(Readdata), .str(memwrite), .clk(clk), .ld(memread),
    .clr(Reset));  // open: sel

  assign MemAddr = Address[6:2];
endmodule

module EXT (
  input  [15:0] imm,
  output [31:0] _0_ext,
  output [31:0] sign_ext,
  output [31:0] shift2,
  output [31:0] shift16
);

  assign _0_ext = {{16{1'b0}}, imm};  // Bit_Extender bit_extender_1
  assign {sign_ext[31:30], shift2[31:2]} = {{16{imm[15]}}, imm};  // Bit_Extender bit_extender_2

  assign shift2[1:0] = 2'b00;
  assign shift16 = {imm, {16{1'b0}}};
  assign sign_ext[29:0] = shift2[31:2];
endmodule

module Controller (
  input  [5:0] op,
  input  [5:0] func,
  output RegWrite,
  output MemRead,
  output MemWrite,
  output RegDst,
  output branch,
  output MemtoReg,
  output [1:0] ALUSrc,
  output [3:0] ALUop
);

  wire addu, beq, lui, lw, not_1_out, not_2_out, not_3_out, not_4_out, not_5_out, not_6_out, not_7_out,
       not_8_out, not_9_out, not_10_out, not_11_out, not_12_out, ori, subu, sw;

  or u_RegWrite (RegWrite, addu, subu, ori, lw, lui);
  buf u_MemRead (MemRead, lw);  // OR_Gate
  not not_1 (not_1_out, op[0]);
  not not_2 (not_2_out, op[1]);
  not not_3 (not_3_out, op[2]);
  not not_4 (not_4_out, op[3]);
  not not_5 (not_5_out, op[4]);
  not not_6 (not_6_out, op[5]);
  not not_7 (not_7_out, func[0]);
  not not_8 (not_8_out, func[1]);
  not not_9 (not_9_out, func[2]);
  not not_10 (not_10_out, func[3]);
  not not_11 (not_11_out, func[4]);
  not not_12 (not_12_out, func[5]);
  buf u_MemWrite (MemWrite, sw);  // OR_Gate
  and u_addu (addu, not_1_out, not_2_out, not_3_out, not_4_out, not_5_out, not_6_out, func[0], not_8_out, not_9_out, not_10_out, not_11_out, func[5]);
  or u_RegDst (RegDst, addu, subu);
  and u_subu (subu, not_1_out, not_2_out, not_3_out, not_4_out, not_5_out, not_6_out, func[0], func[1], not_9_out, not_10_out, not_11_out, func[5]);
  buf u_branch (branch, beq);  // OR_Gate
  and u_ori (ori, op[0], not_2_out, op[2], op[3], not_5_out, not_6_out);
  buf u_MemtoReg (MemtoReg, lw);  // OR_Gate
  and u_lw (lw, op[0], op[1], not_3_out, not_4_out, not_5_out, op[5]);
  or ALUSrc1 (ALUSrc[1], ori, lui);
  and u_sw (sw, op[0], op[1], not_3_out, op[3], not_5_out, op[5]);
  and u_lui (lui, op[0], op[1], op[2], op[3], not_5_out, not_6_out);
  or ALUSrc0 (ALUSrc[0], lw, sw, lui);
  buf ALUop3 (ALUop[3], 1'b0);  // OR_Gate
  and u_beq (beq, not_1_out, not_2_out, op[2], not_4_out, not_5_out, not_6_out);
  or ALUop2 (ALUop[2], subu, beq);
  or ALUop1 (ALUop[1], addu, subu, lw, sw, lui, beq);
  buf ALUop0 (ALUop[0], ori);  // OR_Gate
endmodule

module PCadd (
  input  [31:0] PC,
  input  [31:0] shift2,
  input  PCsrc,
  output [31:0] PC_plus
);

  wire [31:0] adder_1_out, adder_2_out;

  Adder #(.width(32)) adder_1 (.a(PC), .b(32'h4), .out(adder_1_out));  // open: cin, cout
  Adder #(.width(32)) adder_2 (.a(adder_1_out), .b(shift2), .out(adder_2_out));  // open: cin, cout
  Multiplexer #(.width(32), .enable("false")) multiplexer_1 (
    .in0(adder_1_out), .in1(adder_2_out), .out(PC_plus), .sel(PCsrc));
endmodule
