// Logisim project 2.circ as structural Verilog: 1 circuit, main circuit fsm
module fsm (
  input  in_1,
  input  [1:0] in_2,
  output x
);

  wire and_1_out, and_2_out, and_3_out, clock_1_out, not_1_out, not_2_out, not_3_out, not_4_out, not_5_out,
       not_6_out;
  wire [1:0] register_1_q, register_2_q;

  Register #(.width(2)) register_1 (.D(in_2), .Q(register_1_q), .clk(clock_1_out), .clr(and_1_out));  // open: en
  // Probe on register_1_q
  and and_1 (and_1_out, in_1, clock_1_out);
  Clock clock_1 (.out(clock_1_out));
  // Probe on register_2_q
  Register #(.width(2)) register_2 (
    .D(register_1_q), .Q(register_2_q), .clk(clock_1_out), .clr(and_1_out));  // open: en
  not not_1 (not_1_out, in_2[0]);
  not not_2 (not_2_out, register_1_q[0]);
  not not_3 (not_3_out, register_2_q[1]);
  not not_4 (not_4_out, in_2[0]);
  not not_5 (not_5_out, register_1_q[1]);
  not not_6 (not_6_out, register_2_q[1]);
  and and_2 (and_2_out, not_1_out, not_2_out, not_3_out, register_2_q[0]);
  and and_3 (and_3_out, in_2[1], not_4_out, not_5_out, not_6_out, register_2_q[0]);
  or or_1 (x, and_2_out, and_3_out);
endmodule
