// Logisim project alu.circ as structural Verilog: 6 circuits, main circuit alu
module alu (
  input  [3:0] A,
  input  [3:0] B,
  input  [1:0] ALUOp,
  output [3:0] C
);

  wire [3:0] adder_4_1_out_3, and_1_out_3, or_1_out_3, sub_4_1_out_3;

  adder_4 adder_4_1 (.in_1(A), .in_2(B), .out_3(adder_4_1_out_3));
  sub_4 sub_4_1 (.in_1(A), .in_2(B), .out_3(sub_4_1_out_3));
  \and  and_1 (.in_1(A), .in_2(B), .out_3(and_1_out_3));
  \or  or_1 (.in_1(A), .in_2(B), .out_3(or_1_out_3));
  Multiplexer #(.select(2), .width(4), .enable("false")) multiplexer_1 (
    .in0(adder_4_1_out_3), .in1(sub_4_1_out_3), .in2(and_1_out_3), .in3(or_1_out_3), .out(C), .sel(ALUOp));
endmodule

module adder (
  input  a,
  input  b,
  input  c,
  output s,
  output d
);

  wire and_1_out, and_2_out, and_3_out, and_4_out, and_5_out, and_6_out, and_7_out, not_1_out, not_2_out,
       not_3_out, not_4_out, not_5_out, not_6_out;

  not not_1 (not_1_out, a);
  not not_2 (not_2_out, b);
  not not_3 (not_3_out, a);
  not not_4 (not_4_out, c);
  not not_5 (not_5_out, b);
  not not_6 (not_6_out, c);
  and and_1 (and_1_out, b, c);
  and and_2 (and_2_out, a, c);
  and and_3 (and_3_out, a, b);
  and and_4 (and_4_out, not_1_out, not_2_out, c);
  and and_5 (and_5_out, not_3_out, b, not_4_out);
  and and_6 (and_6_out, a, not_5_out, not_6_out);
  and and_7 (and_7_out, a, b, c);
  or or_1 (d, and_1_out, and_2_out, and_3_out);
  or or_2 (s, and_4_out, and_5_out, and_6_out, and_7_out);
endmodule

module adder_4 (
  input  [3:0] in_1,
  input  [3:0] in_2,
  output [3:0] out_3
);

  wire adder_1_d, adder_2_d, adder_3_d;

  adder adder_1 (.a(in_1[0]), .b(in_2[0]), .c(1'b0), .s(out_3[0]), .d(adder_1_d));
  adder adder_2 (.a(in_1[1]), .b(in_2[1]), .c(adder_1_d), .s(out_3[1]), .d(adder_2_d));
  adder adder_3 (.a(in_1[2]), .b(in_2[2]), .c(adder_2_d), .s(out_3[2]), .d(adder_3_d));
  adder adder_4 (.a(in_1[3]), .b(in_2[3]), .c(adder_3_d), .s(out_3[3]));  // open: d
endmodule

module \and  (
  input  [3:0] in_1,
  input  [3:0] in_2,
  output [3:0] out_3
);

  and and_1 (out_3[0], in_1[0], in_2[0]);
  and and_2 (out_3[1], in_1[1], in_2[1]);
  and and_3 (out_3[2], in_2[2], in_1[2]);
  and and_4 (out_3[3], in_1[3], in_2[3]);
endmodule

module \or  (
  input  [3:0] in_1,
  input  [3:0] in_2,
  output [3:0] out_3
);

  or or_1 (out_3[0], in_1[0], in_2[0]);
  or or_2 (out_3[1], in_1[1], in_2[1]);
  or or_3 (out_3[2], in_2[2], in_1[2]);
  or or_4 (out_3[3], in_1[3], in_2[3]);
endmodule

module sub_4 (
  input  [3:0] in_1,
  input  [3:0] in_2,
  output [3:0] out_3
);

  wire adder_1_d, adder_2_d, adder_3_d, not_1_out, not_2_out, not_3_out, not_4_out;

  adder adder_1 (.a(in_1[0]), .b(not_1_out), .c(1'b1), .s(out_3[0]), .d(adder_1_d));
  not not_1 (not_1_out, in_2[0]);
  not not_2 (not_2_out, in_2[2]);
  not not_3 (not_3_out, in_2[1]);
  not not_4 (not_4_out, in_2[3]);
  adder adder_2 (.a(in_1[1]), .b(not_3_out), .c(adder_1_d), .s(out_3[1]), .d(adder_2_d));
  adder adder_3 (.a(in_1[2]), .b(not_2_out), .c(adder_2_d), .s(out_3[2]), .d(adder_3_d));
  adder adder_4 (.a(in_1[3]), .b(not_4_out), .c(adder_3_d), .s(out_3[3]));  // open: d
endmodule
