// Logisim project moore.circ as structural Verilog: 1 circuit, main circuit moore
module moore (
  input  TA,
  input  TB,
  input  in_3,
  input  in_4,
  input  in_5,
  output [1:0] out_6,
  output [1:0] out_7
);

  wire and_1_out, and_2_out, clock_1_out, d_ff_1_q, not_1_out, not_2_out, not_3_out, not_4_out, not_5_out,
       not_6_out, or_1_out, xor_1_out;

  not not_1 (not_1_out, TA);
  not not_2 (not_2_out, d_ff_1_q);
  not not_3 (not_3_out, out_6[1]);
  not not_4 (not_4_out, d_ff_1_q);
  not not_5 (not_5_out, TB);
  Clock clock_1 (.out(clock_1_out));
  and and_1 (and_1_out, not_1_out, not_2_out, not_3_out);
  and and_2 (and_2_out, not_4_out, not_5_out, out_6[1]);
  or or_1 (or_1_out, and_1_out, and_2_out);
  xor xor_1 (xor_1_out, d_ff_1_q, out_6[1]);
  D_Flip_Flop d_ff_1 (
    .clk(clock_1_out), .D(or_1_out), .Q(d_ff_1_q), .preset(in_3), .en(in_4), .reset(in_5));  // open: Qn
  D_Flip_Flop d_ff_2 (
    .clk(clock_1_out), .D(xor_1_out), .Q(out_6[1]), .preset(in_3), .en(in_4), .reset(in_5));  // open: Qn
  not not_6 (not_6_out, out_6[1]);
  not not_7 (out_7[1], d_ff_1_q);
  and and_3 (out_6[0], not_6_out, d_ff_1_q);
  and and_4 (out_7[0], out_6[1], d_ff_1_q);
endmodule
