// Logisim project 四分投币.circ as structural Verilog: 3 circuits, main circuit main
module main (
  input  in,
  output \output ,
  output change
);

  wire clock_1_out, d_ff_1_q, not_1_out;
  wire [1:0] n1_1_c0, register_1_q;

  Clock clock_1 (.out(clock_1_out));
  _1 u_1_1 (.s1(register_1_q[1]), .s0(register_1_q[0]), .i(in), .c1(n1_1_c0[1]), .c0(n1_1_c0[0]));
  Register #(.width(2)) register_1 (.D(n1_1_c0), .Q(register_1_q), .clk(clock_1_out), .clr(d_ff_1_q));  // open: en
  D_Flip_Flop d_ff_1 (.clk(clock_1_out), .D(\output ), .Q(d_ff_1_q), .reset(not_1_out));  // open: Qn, preset, en
  not not_1 (not_1_out, \output );
  _2 u_2_1 (.c1(register_1_q[1]), .c0(register_1_q[0]), .i(in), .\output (\output ), .change(change));
endmodule

module _1 (
  input  s1,
  input  s0,
  input  i,
  output c1,
  output c0
);

  wire and_1_out, and_2_out, and_3_out, and_4_out, and_5_out, not_1_out, not_2_out, not_3_out, not_4_out,
       not_5_out, not_6_out, not_7_out;

  not not_1 (not_1_out, s1);
  not not_2 (not_2_out, s1);
  not not_3 (not_3_out, s0);
  not not_4 (not_4_out, i);
  not not_5 (not_5_out, s0);
  not not_6 (not_6_out, i);
  not not_7 (not_7_out, s1);
  and and_1 (and_1_out, not_1_out, i);
  and and_2 (and_2_out, not_2_out, s0);
  and and_3 (and_3_out, s1, not_3_out, not_4_out);
  and and_4 (and_4_out, not_5_out, not_6_out);
  and and_5 (and_5_out, not_7_out, s0, i);
  or or_1 (c1, and_1_out, and_2_out, and_3_out);
  or or_2 (c0, and_4_out, and_5_out);
endmodule

module _2 (
  input  c1,
  input  c0,
  input  i,
  output \output ,
  output change
);

  wire and_1_out, and_2_out;

  and and_1 (and_1_out, c1, i);
  and and_2 (and_2_out, c1, c0);
  and and_3 (change, c1, c0, i);
  or or_1 (\output , and_1_out, and_2_out);
endmodule
