// Logisim project 0.circ as structural Verilog: 1 circuit, main circuit fsm
module fsm (
  input  CLR,
  input  [1:0] In,
  output out_3
);

  wire a, and_1_out, and_2_out, and_3_out, and_4_out, and_5_out, and_6_out, and_7_out, and_8_out, and_9_out,
       and_10_out, b, CLK_out, d_ff_1_q, d_ff_1_qn, d_ff_2_qn, na, nb, nc, nd, or_1_out, or_2_out,
       register_3_q, register_4_q;

  Clock CLK (.out(CLK_out));
  not not_1 (nc, In[1]);
  not not_2 (nd, In[0]);
  and and_1 (and_1_out, na, nb, nc, In[0]);
  and and_2 (and_2_out, a, nb, nc, nd);
  and and_3 (and_3_out, a, nb, In[1], nd);
  and and_4 (and_4_out, a, b, nc, In[0]);
  or or_1 (or_1_out, and_1_out, and_2_out, and_3_out, and_4_out);
  and and_5 (and_5_out, na, b, nc, In[0]);
  and and_6 (and_6_out, a, nb, nc);
  and and_7 (and_7_out, a, nb, In[1], nd);
  or or_2 (or_2_out, and_5_out, and_6_out, and_7_out);
  Register #(.width(1)) register_1 (.D(or_2_out), .en(1'b1), .Q(a), .clk(CLK_out), .clr(and_8_out));
  and and_8 (and_8_out, CLR, CLK_out);
  not not_3 (na, a);
  not not_4 (nb, b);
  Register #(.width(1)) register_2 (.D(or_1_out), .en(1'b1), .Q(b), .clk(CLK_out), .clr(and_8_out));
  Register #(.width(1)) register_3 (.D(a), .en(1'b1), .Q(register_3_q), .clk(CLK_out), .clr(and_8_out));
  Register #(.width(1)) register_4 (.D(b), .en(1'b1), .Q(register_4_q), .clk(CLK_out), .clr(and_8_out));
  D_Flip_Flop d_ff_1 (
    .clk(CLK_out), .D(In[1]), .Q(d_ff_1_q), .Qn(d_ff_1_qn), .en(1'b1), .reset(and_8_out));  // open: preset
  D_Flip_Flop d_ff_2 (.clk(CLK_out), .D(In[0]), .Qn(d_ff_2_qn), .en(1'b1), .reset(and_8_out));  // open: Q, preset
  and and_9 (and_9_out, register_3_q, register_4_q, d_ff_1_qn, d_ff_2_qn);
  and and_10 (and_10_out, register_3_q, register_4_q, d_ff_1_q, d_ff_2_qn);
  or or_3 (out_3, and_9_out, and_10_out);

  // Other names for the same wires on the sheet: d = In[0]; c = In[1]

  // Notes on the sheet:
  //   c
  //   d
  //   bb
  //   aa
  //   a
  //   b
endmodule
