// Logisim project 3.circ as structural Verilog: 1 circuit, main circuit fsm
module fsm (
  input  in_1,
  input  [1:0] in_2,
  output out_3
);

  wire ac, and_1_out, b, clock_1_out, d_ff_1_q, not_1_out, not_2_out, not_3_out, register_1_q, register_2_q;

  D_Flip_Flop d_ff_1 (.clk(clock_1_out), .D(in_1), .Q(d_ff_1_q), .reset(not_1_out));  // open: Qn, preset, en
  not not_1 (not_1_out, in_1);
  Multiplexer #(.select(2), .enable("false")) multiplexer_1 (
    .in0(1'b0), .in1(1'b1), .in2(1'b0), .in3(1'b0), .out(b), .sel(in_2));
  Multiplexer #(.select(2), .enable("false")) multiplexer_2 (
    .in0(1'b1), .in1(1'b0), .in2(1'b1), .in3(1'b0), .out(ac), .sel(in_2));
  Clock clock_1 (.out(clock_1_out));
  not not_2 (not_2_out, register_1_q);
  and and_1 (and_1_out, not_2_out, register_2_q, ac);
  Register #(.width(1)) register_1 (.D(and_1_out), .Q(register_1_q), .clk(clock_1_out), .clr(d_ff_1_q));  // open: en
  Register #(.width(1)) register_2 (.D(b), .Q(register_2_q), .clk(clock_1_out), .clr(d_ff_1_q));  // open: en
  not not_3 (not_3_out, register_2_q);
  and and_2 (out_3, register_1_q, not_3_out, ac);
endmodule
