// Logisim project 4.1.circ as structural Verilog: 3 circuits, main circuit main
module main (
  input  in_1,
  input  in_2,
  input  in_3,
  input  in_4,
  input  in_5,
  input  in_6,
  input  in_7,
  input  in_8,
  input  in_9,
  input  in_10,
  input  in_11,
  input  [1:0] in_12,
  input  [3:0] in_13,
  output out_14,
  output out_15,
  output out_16,
  output out_17,
  output out_18,
  output out_19,
  output out_20,
  output out_21,
  output out_22,
  output out_23
);

  Multiplexer #(.select(2)) multiplexer_1 (
    .in0(in_1), .in1(in_3), .in2(in_4), .in3(in_6), .out(out_18), .sel(in_12), .en(in_10));
  Decoder #(.select(2)) decoder_1 (.out0(out_20), .out1(out_21), .out2(out_22), .out3(out_23), .sel(in_12), .en(in_10));
  Demultiplexer #(.select(2)) demultiplexer_1 (
    .out0(out_14), .out1(out_15), .out2(out_16), .out3(out_17), .in(in_2), .sel(in_13[1:0]), .en(in_11));
  Multiplexer #(.select(2)) multiplexer_2 (
    .in0(in_5), .in1(in_7), .in2(in_8), .in3(in_9), .out(out_19), .sel(in_13[3:2]), .en(in_11));
endmodule

module _2_1 (
  input  in_1,
  input  in_2,
  input  select,
  output out_4
);

  wire and_1_out, and_2_out, not_1_out;

  not not_1 (not_1_out, select);
  and and_1 (and_1_out, in_1, not_1_out);
  and and_2 (and_2_out, in_2, select);
  or or_1 (out_4, and_1_out, and_2_out);
endmodule

module _4_1 (
  input  in_1,
  input  in_2,
  input  in_3,
  input  in_4,
  input  in_5,
  input  in_6,
  output out_7
);

  wire n2_1_1_out_4, n2_1_2_out_4;

  _2_1 u_2_1_1 (.in_1(in_1), .in_2(in_2), .out_4(n2_1_1_out_4), .select(in_6));
  _2_1 u_2_1_2 (.in_1(in_3), .in_2(in_4), .out_4(n2_1_2_out_4), .select(in_6));
  _2_1 u_2_1_3 (.in_1(n2_1_1_out_4), .in_2(n2_1_2_out_4), .out_4(out_7), .select(in_5));
endmodule
