// Logisim project 4bit_sort.circ as structural Verilog: 3 circuits, main circuit 1bit_swap
module _1bit_swap (
  input  [3:0] in_1,
  input  [3:0] in_2,
  input  in_3,
  output [3:0] out_4,
  output [3:0] out_5
);

  wire [3:0] and_1_out, and_2_out, and_3_out, and_4_out, bit_extender_1_out, not_1_out, not_2_out;

  assign bit_extender_1_out = {{3{in_3}}, in_3};  // Bit_Extender bit_extender_1
  assign not_1_out = ~bit_extender_1_out;  // NOT_Gate not_1, 4 bits wide
  assign not_2_out = ~bit_extender_1_out;  // NOT_Gate not_2, 4 bits wide
  assign and_1_out = in_1 & not_1_out;  // AND_Gate and_1, 4 bits wide
  assign and_2_out = in_2 & bit_extender_1_out;  // AND_Gate and_2, 4 bits wide
  assign and_3_out = bit_extender_1_out & in_1;  // AND_Gate and_3, 4 bits wide
  assign and_4_out = in_2 & not_2_out;  // AND_Gate and_4, 4 bits wide
  assign out_4 = and_1_out | and_2_out;  // OR_Gate or_1, 4 bits wide
  assign out_5 = and_3_out | and_4_out;  // OR_Gate or_2, 4 bits wide
endmodule

module _4bit_swap (
  input  [3:0] in_1,
  input  [3:0] in_2,
  input  [3:0] in_3,
  input  [3:0] in_4,
  input  in_5,
  input  in_6,
  output [3:0] out_7,
  output [3:0] out_8,
  output [3:0] out_9,
  output [3:0] out_10
);

  _1bit_swap u_1bit_swap_1 (.in_1(in_1), .in_2(in_2), .in_3(in_5), .out_4(out_7), .out_5(out_8));
  _1bit_swap u_1bit_swap_2 (.in_1(in_3), .in_2(in_4), .in_3(in_6), .out_4(out_9), .out_5(out_10));
endmodule

module _4bit_sort (
  input  [3:0] A,
  input  [3:0] B,
  input  [3:0] C,
  input  [3:0] D,
  output [3:0] _1,
  output [3:0] _2,
  output [3:0] _3,
  output [3:0] _4
);

  wire comparator_1_lt, comparator_2_lt, comparator_3_lt, comparator_4_lt, comparator_5_lt, not_1_out,
       not_2_out, not_3_out, not_4_out, not_5_out;
  wire [3:0] n4bit_swap_1_out_7, n4bit_swap_1_out_8, n4bit_swap_1_out_9, n4bit_swap_1_out_10,
       n4bit_swap_2_out_8, n4bit_swap_2_out_9;

  Comparator #(.width(4), .mode("unsigned")) comparator_1 (.a(A), .b(B), .lt(comparator_1_lt));  // open: gt, eq
  not not_1 (not_1_out, comparator_1_lt);
  Comparator #(.width(4), .mode("unsigned")) comparator_2 (.a(C), .b(D), .lt(comparator_2_lt));  // open: gt, eq
  not not_2 (not_2_out, comparator_2_lt);
  _4bit_swap u_4bit_swap_1 (
    .in_1(A), .in_2(B), .in_3(C), .in_4(D), .in_5(not_1_out), .in_6(not_2_out), .out_7(n4bit_swap_1_out_7),
    .out_8(n4bit_swap_1_out_8), .out_9(n4bit_swap_1_out_9), .out_10(n4bit_swap_1_out_10));
  Comparator #(.width(4), .mode("unsigned")) comparator_3 (
    .a(n4bit_swap_1_out_7), .b(n4bit_swap_1_out_9), .lt(comparator_3_lt));  // open: gt, eq
  Comparator #(.width(4), .mode("unsigned")) comparator_4 (
    .a(n4bit_swap_1_out_8), .b(n4bit_swap_1_out_10), .lt(comparator_4_lt));  // open: gt, eq
  not not_3 (not_3_out, comparator_3_lt);
  not not_4 (not_4_out, comparator_4_lt);
  _4bit_swap u_4bit_swap_2 (
    .in_1(n4bit_swap_1_out_7), .in_2(n4bit_swap_1_out_9), .in_3(n4bit_swap_1_out_8),
    .in_4(n4bit_swap_1_out_10), .in_5(not_3_out), .in_6(not_4_out), .out_7(_1), .out_8(n4bit_swap_2_out_8),
    .out_9(n4bit_swap_2_out_9), .out_10(_4));
  Comparator #(.width(4), .mode("unsigned")) comparator_5 (
    .a(n4bit_swap_2_out_8), .b(n4bit_swap_2_out_9), .lt(comparator_5_lt));  // open: gt, eq
  not not_5 (not_5_out, comparator_5_lt);
  _1bit_swap u_1bit_swap_1 (
    .in_1(n4bit_swap_2_out_8), .in_2(n4bit_swap_2_out_9), .in_3(not_5_out), .out_4(_2), .out_5(_3));
endmodule
