// Logisim project CRC.circ as structural Verilog: 2 circuits, main circuit CRC
module CRC (
  input  [7:0] in_1,
  input  [3:0] in_2,
  output [10:0] out_3
);

  wire [2:0] n1_1_out_3, n1_2_out_3, n1_3_out_3, n1_4_out_3, n1_5_out_3, n1_6_out_3, n1_7_out_3;

  // Probe on in_1[7:4]
  _1 u_1_1 (.A(in_1[7:4]), .B(in_2), .out_3(n1_1_out_3));
  // Probe on {n1_1_out_3, in_1[3]}
  _1 u_1_2 (.A({n1_1_out_3, in_1[3]}), .B(in_2), .out_3(n1_2_out_3));
  // Probe on {n1_2_out_3, in_1[2]}
  // Probe on {n1_3_out_3, in_1[1]}
  _1 u_1_3 (.A({n1_2_out_3, in_1[2]}), .B(in_2), .out_3(n1_3_out_3));
  _1 u_1_4 (.A({n1_3_out_3, in_1[1]}), .B(in_2), .out_3(n1_4_out_3));
  // Probe on {n1_4_out_3, in_1[0]}
  _1 u_1_5 (.A({n1_4_out_3, in_1[0]}), .B(in_2), .out_3(n1_5_out_3));
  // Probe on {n1_5_out_3, 1'b0}
  _1 u_1_6 (.A({n1_5_out_3, 1'b0}), .B(in_2), .out_3(n1_6_out_3));
  // Probe on {n1_6_out_3, 1'b0}
  // Probe on {n1_7_out_3, 1'b0}
  _1 u_1_7 (.A({n1_6_out_3, 1'b0}), .B(in_2), .out_3(n1_7_out_3));
  _1 u_1_8 (.A({n1_7_out_3, 1'b0}), .B(in_2), .out_3(out_3[2:0]));
  // Probe on out_3[2:0]

  assign out_3[10:3] = in_1;
endmodule

module _1 (
  input  [3:0] A,
  input  [3:0] B,
  output [2:0] out_3
);

  wire not_1_out;
  wire [2:0] xor_1_out;

  xor xor_1 (xor_1_out[0], A[0], B[0]);
  xor xor_2 (xor_1_out[1], B[1], A[1]);
  xor xor_3 (xor_1_out[2], A[2], B[2]);
  Multiplexer #(.width(3), .enable("false")) multiplexer_1 (
    .in0(xor_1_out), .in1(A[2:0]), .out(out_3), .sel(not_1_out));
  not not_1 (not_1_out, A[3]);
endmodule
