// Logisim project adder.circ as structural Verilog: 3 circuits, main circuit adder0
module adder0 (
  input  A,
  input  B,
  output S0,
  output C0
);

  wire and_1_out, and_2_out, not_1_out, not_2_out;

  not not_1 (not_1_out, A);
  not not_2 (not_2_out, B);
  and and_1 (and_1_out, not_1_out, B);
  and and_2 (and_2_out, A, not_2_out);
  and and_3 (C0, A, B);
  or or_1 (S0, and_1_out, and_2_out);
endmodule

module adder1 (
  input  A,
  input  B,
  input  C,
  output S0,
  output C0
);

  wire and_1_out, and_2_out, and_3_out, and_4_out, and_5_out, and_6_out, and_7_out, not_1_out, not_2_out,
       not_3_out, not_4_out, not_5_out, not_6_out;

  not not_1 (not_1_out, A);
  not not_2 (not_2_out, B);
  and and_1 (and_1_out, not_1_out, not_2_out, C);
  not not_3 (not_3_out, A);
  and and_2 (and_2_out, not_3_out, B, not_4_out);
  not not_4 (not_4_out, C);
  and and_3 (and_3_out, A, not_5_out, not_6_out);
  not not_5 (not_5_out, B);
  not not_6 (not_6_out, C);
  and and_4 (and_4_out, A, B, C);
  and and_5 (and_5_out, B, C);
  and and_6 (and_6_out, A, C);
  and and_7 (and_7_out, A, B);
  or or_1 (S0, and_1_out, and_2_out, and_3_out, and_4_out);
  or or_2 (C0, and_5_out, and_6_out, and_7_out);
endmodule

module adder_4 (
  input  in_1,
  input  [3:0] in_2,
  input  [3:0] in_3,
  output [4:0] out_4
);

  wire adder1_1_c0, adder1_2_c0, adder1_3_c0;

  adder1 adder1_1 (.A(in_2[0]), .B(in_3[0]), .C(in_1), .S0(out_4[0]), .C0(adder1_1_c0));
  adder1 adder1_2 (.A(in_2[1]), .B(in_3[1]), .C(adder1_1_c0), .S0(out_4[1]), .C0(adder1_2_c0));
  adder1 adder1_3 (.A(in_2[2]), .B(in_3[2]), .C(adder1_2_c0), .S0(out_4[2]), .C0(adder1_3_c0));
  adder1 adder1_4 (.A(in_2[3]), .B(in_3[3]), .C(adder1_3_c0), .S0(out_4[3]), .C0(out_4[4]));
endmodule
