// Logisim project feibonaqie.circ as structural Verilog: 2 circuits, main circuit main
module main (
  input  [2:0] in_1,
  output [3:0] out_2
);

  wire clock_1_out, comparator_1_gt;
  wire [2:0] counter_1_q;
  wire [3:0] multiplexer_1_out, n1_1_out_4, register_1_q, register_2_q, register_3_q;

  Clock clock_1 (.out(clock_1_out));
  Counter #(.width(3), .max('h7), .ongoal("stay")) counter_1 (
    .Q(counter_1_q), .clk(clock_1_out));  // open: load, D, count, carry, clr
  Comparator #(.width(3), .mode("unsigned")) comparator_1 (
    .a(in_1), .b(counter_1_q), .gt(comparator_1_gt));  // open: eq, lt
  _1 u_1_1 (.in_1(register_2_q), .in_2(register_3_q), .in_3(counter_1_q), .out_4(n1_1_out_4));
  Register #(.width(4)) register_1 (.D(4'b0001), .Q(register_1_q), .clk(clock_1_out));  // open: en, clr
  Register #(.width(4)) register_2 (
    .D(n1_1_out_4), .en(comparator_1_gt), .Q(register_2_q), .clk(clock_1_out));  // open: clr
  Register #(.width(4)) register_3 (
    .D(register_2_q), .en(comparator_1_gt), .Q(register_3_q), .clk(clock_1_out));  // open: clr
  Multiplexer #(.width(4), .enable("false")) multiplexer_1 (
    .in0(n1_1_out_4), .in1(4'b0000), .out(multiplexer_1_out), .sel(comparator_1_gt));
  Multiplexer #(.select(3), .width(4), .enable("false")) multiplexer_2 (
    .in0(4'b0000), .in1(register_1_q), .in2(multiplexer_1_out), .in3(multiplexer_1_out),
    .in4(multiplexer_1_out), .in5(multiplexer_1_out), .in6(multiplexer_1_out), .in7(multiplexer_1_out),
    .out(out_2), .sel(in_1));
endmodule

module _1 (
  input  [3:0] in_1,
  input  [3:0] in_2,
  input  [2:0] in_3,
  output [3:0] out_4
);

  wire comparator_1_eq;
  wire [3:0] adder_1_out;

  Adder #(.width(4)) adder_1 (.a(in_1), .b(in_2), .out(adder_1_out));  // open: cin, cout
  Comparator #(.width(3)) comparator_1 (.a(in_3), .b(3'b001), .eq(comparator_1_eq));  // open: gt, lt
  Multiplexer #(.width(4), .enable("false")) multiplexer_1 (
    .in0(adder_1_out), .in1(4'b0001), .out(out_4), .sel(comparator_1_eq));
endmodule
