// Logisim project feibonaqie64.circ as structural Verilog: 2 circuits, main circuit main
module main (
  input  [31:0] in_1,
  output [31:0] out_2
);

  wire clock_1_out, comparator_1_gt;
  wire [1:0] comparator_2_eq;
  wire [31:0] counter_1_q, multiplexer_1_out, n1_1_out_4, register_1_q, register_2_q, register_3_q;

  Clock clock_1 (.out(clock_1_out));
  Counter #(.width(32), .max('hffffffff), .ongoal("stay")) counter_1 (
    .Q(counter_1_q), .clk(clock_1_out));  // open: load, D, count, carry, clr
  Comparator #(.width(32), .mode("unsigned")) comparator_1 (
    .a(in_1), .b(counter_1_q), .gt(comparator_1_gt));  // open: eq, lt
  Comparator #(.width(32)) comparator_2 (.a(in_1), .b({32{1'b0}}), .eq(comparator_2_eq[0]));  // open: gt, lt
  Comparator #(.width(32)) comparator_3 (.a(in_1), .b(32'h1), .eq(comparator_2_eq[1]));  // open: gt, lt
  _1 u_1_1 (.in_1(register_2_q), .in_2(register_3_q), .in_3(counter_1_q), .out_4(n1_1_out_4));
  Register #(.width(32)) register_1 (.D(32'h1), .Q(register_1_q), .clk(clock_1_out));  // open: en, clr
  Register #(.width(32)) register_2 (
    .D(n1_1_out_4), .en(comparator_1_gt), .Q(register_2_q), .clk(clock_1_out));  // open: clr
  Register #(.width(32)) register_3 (
    .D(register_2_q), .en(comparator_1_gt), .Q(register_3_q), .clk(clock_1_out));  // open: clr
  Multiplexer #(.width(32), .enable("false")) multiplexer_1 (
    .in0(n1_1_out_4), .in1({32{1'b0}}), .out(multiplexer_1_out), .sel(comparator_1_gt));
  Multiplexer #(.select(2), .width(32), .enable("false")) multiplexer_2 (
    .in0(multiplexer_1_out), .in1({32{1'b0}}), .in2(register_1_q), .out(out_2), .sel(comparator_2_eq));  // open: in3
endmodule

module _1 (
  input  [31:0] in_1,
  input  [31:0] in_2,
  input  [31:0] in_3,
  output [31:0] out_4
);

  wire comparator_1_eq;
  wire [31:0] adder_1_out;

  Adder #(.width(32)) adder_1 (.a(in_1), .b(in_2), .out(adder_1_out));  // open: cin, cout
  Comparator #(.width(32)) comparator_1 (.a(in_3), .b(32'h1), .eq(comparator_1_eq));  // open: gt, lt
  Multiplexer #(.width(32), .enable("false")) multiplexer_1 (
    .in0(adder_1_out), .in1(32'h1), .out(out_4), .sel(comparator_1_eq));
endmodule
