// Logisim project fsm.circ as structural Verilog: 3 circuits, main circuit fsm
module fsm (
  input  in_1,
  input  [1:0] in_2,
  output out_3
);

  wire clock_1_out, d_ff_1_q, not_1_out;
  wire [1:0] n1_1_c0, register_1_q;

  Clock clock_1 (.out(clock_1_out));
  _1 u_1_1 (.a1(register_1_q[1]), .a0(register_1_q[0]), .b1(in_2[1]), .b0(in_2[0]), .c1(n1_1_c0[1]), .c0(n1_1_c0[0]));
  D_Flip_Flop d_ff_1 (.clk(clock_1_out), .D(in_1), .Q(d_ff_1_q), .reset(not_1_out));  // open: Qn, preset, en
  not not_1 (not_1_out, in_1);
  Register #(.width(2)) register_1 (.D(n1_1_c0), .Q(register_1_q), .clk(clock_1_out), .clr(d_ff_1_q));  // open: en
  _2 u_2_1 (.a1(register_1_q[1]), .a0(register_1_q[0]), .b1(in_2[1]), .b0(in_2[0]), .out(out_3));
endmodule

module _1 (
  input  a1,
  input  a0,
  input  b1,
  input  b0,
  output c1,
  output c0
);

  wire and_1_out, and_2_out, and_3_out, and_4_out, not_1_out, not_2_out, not_3_out, not_4_out, not_5_out,
       not_6_out, not_7_out;

  not not_1 (not_1_out, a1);
  and and_1 (and_1_out, not_1_out, a0, not_2_out);
  not not_2 (not_2_out, b0);
  and and_2 (and_2_out, a1, not_3_out, not_4_out);
  not not_3 (not_3_out, a0);
  not not_4 (not_4_out, b0);
  not not_5 (not_5_out, b1);
  and and_3 (and_3_out, not_5_out, b0);
  and and_4 (and_4_out, a1, not_6_out, not_7_out);
  not not_6 (not_6_out, a0);
  not not_7 (not_7_out, b0);
  or or_1 (c1, and_1_out, and_2_out);
  or or_2 (c0, and_3_out, and_4_out);
endmodule

module _2 (
  input  a1,
  input  a0,
  input  b1,
  input  b0,
  output out
);

  wire not_1_out, not_2_out;

  and and_1 (out, a1, not_1_out, not_2_out);
  not not_1 (not_1_out, a0);
  not not_2 (not_2_out, b0);
endmodule
