// Logisim project mod.circ as structural Verilog: 3 circuits, main circuit mod5
module mod5 (
  input  in_1,
  output out_2,
  output out_3,
  output out_4,
  output out_5,
  output out_6
);

  wire clock_1_out;
  wire [1:0] n1_1_a0, n2_1_a0, register_1_q;

  Clock clock_1 (.out(clock_1_out));
  _1 u_1_1 (.s1(register_1_q[1]), .s0(register_1_q[0]), .b(in_1), .a0(n1_1_a0[0]), .a1(n1_1_a0[1]));
  Register #(.width(2)) register_1 (.D(n1_1_a0), .Q(register_1_q), .clk(clock_1_out));  // open: en, clr
  _2 u_2_1 (.s1(register_1_q[1]), .s0(register_1_q[0]), .b(in_1), .a0(n2_1_a0[0]), .a1(n2_1_a0[1]));
  Decoder #(.select(2), .enable("false")) decoder_1 (
    .out0(out_3), .out1(out_4), .out2(out_5), .out3(out_6), .sel(n2_1_a0));

  assign out_2 = 1'b0;
endmodule

module _1 (
  input  s1,
  input  s0,
  input  b,
  output a0,
  output a1
);

  wire and_1_out, and_2_out, and_3_out, and_4_out, and_5_out, and_6_out, not_1_out, not_2_out, not_3_out,
       not_4_out, not_5_out, not_6_out, not_7_out, not_8_out;

  not not_1 (not_1_out, s1);
  not not_2 (not_2_out, s0);
  not not_3 (not_3_out, s1);
  not not_4 (not_4_out, s0);
  not not_5 (not_5_out, s1);
  not not_6 (not_6_out, b);
  not not_7 (not_7_out, s0);
  not not_8 (not_8_out, b);
  and and_1 (and_1_out, not_1_out, s0);
  and and_2 (and_2_out, s1, not_2_out);
  and and_3 (and_3_out, not_3_out, not_4_out, b);
  and and_4 (and_4_out, not_5_out, s0, not_6_out);
  and and_5 (and_5_out, s1, not_7_out, not_8_out);
  and and_6 (and_6_out, s1, s0, b);
  or or_1 (a1, and_1_out, and_2_out);
  or or_2 (a0, and_3_out, and_4_out, and_5_out, and_6_out);
endmodule

module _2 (
  input  s1,
  input  s0,
  input  b,
  output a0,
  output a1
);

  wire and_1_out, and_2_out, and_3_out, and_4_out, and_5_out, and_6_out, not_1_out, not_2_out, not_3_out,
       not_4_out, not_5_out, not_6_out, not_7_out, not_8_out;

  not not_1 (not_1_out, s1);
  not not_2 (not_2_out, s0);
  not not_3 (not_3_out, s1);
  not not_4 (not_4_out, s0);
  not not_5 (not_5_out, s1);
  not not_6 (not_6_out, b);
  not not_7 (not_7_out, s0);
  not not_8 (not_8_out, b);
  and and_1 (and_1_out, not_1_out, s0);
  and and_2 (and_2_out, s1, not_2_out);
  and and_3 (and_3_out, not_3_out, not_4_out, b);
  and and_4 (and_4_out, not_5_out, s0, not_6_out);
  and and_5 (and_5_out, s1, not_7_out, not_8_out);
  and and_6 (and_6_out, s1, s0, b);
  or or_1 (a1, and_1_out, and_2_out);
  or or_2 (a0, and_3_out, and_4_out, and_5_out, and_6_out);
endmodule
