// Logisim project p0.4.circ as structural Verilog: 1 circuit, main circuit fsm
module fsm (
  input  in_1,
  input  [1:0] in_2,
  output out_3
);

  wire clock_1_out, decoder_1_out0, decoder_1_out2, decoder_2_out0, decoder_2_out2, decoder_3_out1, or_1_out,
       or_2_out;
  wire [1:0] and_1_out, and_2_out, register_1_q, register_2_q;
  wire [1:1] not_1_out;

  not not_1 (not_1_out[1], in_1);
  assign and_1_out = in_2 & {2{not_1_out[1]}};  // AND_Gate and_1, 2 bits wide
  Clock clock_1 (.out(clock_1_out));
  Register #(.width(2)) register_1 (.D(and_1_out), .Q(register_1_q), .clk(clock_1_out));  // open: en, clr
  assign and_2_out = register_1_q & {2{not_1_out[1]}};  // AND_Gate and_2, 2 bits wide
  Decoder #(.select(2)) decoder_1 (.out0(decoder_1_out0), .out2(decoder_1_out2), .sel(in_2));  // open: out1, out3, en
  Register #(.width(2)) register_2 (.D(and_2_out), .Q(register_2_q), .clk(clock_1_out));  // open: en, clr
  Decoder #(.select(2)) decoder_2 (
    .out0(decoder_2_out0), .out2(decoder_2_out2), .sel(register_1_q));  // open: out1, out3, en
  Decoder #(.select(2)) decoder_3 (.out1(decoder_3_out1), .sel(register_2_q));  // open: out0, out2, out3, en
  or or_1 (or_1_out, decoder_1_out0, decoder_1_out2);
  or or_2 (or_2_out, decoder_2_out0, decoder_2_out2);
  and and_3 (out_3, or_1_out, or_2_out, decoder_3_out1);
endmodule
