// Logisim project p0.4second.circ as structural Verilog: 1 circuit, main circuit fsm
module fsm (
  input  in_1,
  input  [1:0] in_2,
  output x
);

  wire and_3_out, and_4_out, and_5_out, clock_1_out, not_2_out, not_3_out, not_4_out, not_5_out, not_6_out,
       not_7_out, not_8_out;
  wire [1:0] and_1_out, and_2_out, register_1_q, register_2_q;
  wire [1:1] not_1_out;

  not not_1 (not_1_out[1], in_1);
  Register #(.width(2)) register_1 (.D(and_1_out), .Q(register_1_q), .clk(clock_1_out));  // open: en, clr
  assign and_1_out = {2{not_1_out[1]}} & in_2;  // AND_Gate and_1, 2 bits wide
  Clock clock_1 (.out(clock_1_out));
  assign and_2_out = register_1_q & {2{not_1_out[1]}};  // AND_Gate and_2, 2 bits wide
  Register #(.width(2)) register_2 (.D(and_2_out), .Q(register_2_q), .clk(clock_1_out));  // open: en, clr
  not not_2 (not_2_out, in_2[0]);
  not not_3 (not_3_out, register_1_q[0]);
  not not_4 (not_4_out, register_2_q[1]);
  not not_5 (not_5_out, in_2[0]);
  not not_6 (not_6_out, register_1_q[1]);
  not not_7 (not_7_out, register_2_q[1]);
  not not_8 (not_8_out, in_2[0]);
  and and_3 (and_3_out, not_2_out, not_3_out, not_4_out, register_2_q[0]);
  and and_4 (and_4_out, in_2[1], not_5_out, not_6_out, not_7_out, register_2_q[0]);
  and and_5 (and_5_out, in_2[1], not_8_out);
  or or_1 (x, and_5_out, and_3_out, and_4_out);
endmodule
