// Logisim project sr锁存器.circ as structural Verilog: 1 circuit, main circuit main
module main (
  input  S,
  input  CP,
  input  R,
  output Q,
  output QN
);

  wire nand_1_out, nand_2_out;

  nand nand_1 (nand_1_out, S, CP);
  nand nand_2 (nand_2_out, CP, R);
  // Probe on nand_1_out
  // Probe on nand_2_out
  nand nand_3 (Q, nand_1_out, QN);
  nand nand_4 (QN, Q, nand_2_out);
endmodule
